# Fritzing sketch wemos - Rele (saved by Fritzing 0.9.10b)

parts:
  KY-1 = Keyes Relay [package=THT]
  Componente1 = Arduino Uno (Rev3)
  M1 = >Wemos D1 R32
  Mod1 = Arduino Sensor Shield v5.0
  U1 = Vibration Motor- ROB-08449 [package=vibe-motor-10mm]

nets:
  N1: KY-1.signal, Mod1.2-S, Mod1.ParallelLCD-D2
  N2: KY-1.power, KY-1.C, Mod1.VCC, Mod1.2-V
  N3: KY-1.ground, Mod1.GND, Mod1.2-G, U1.+
  N4: KY-1.NO, U1.-
  N5: Componente1.A0, M1.IO2
  N6: Componente1.A1, M1.IO4
  N7: Componente1.A2, M1.IO35
  N8: Componente1.A3, M1.IO34
  N9: Componente1.A4/SDA, M1.IO36, M1.SDA
  N10: Componente1.A5/SCL, M1.IO39, M1.SCL
  N11: Componente1.D8, M1.IO12
  N12: Componente1.D9_PWM, M1.IO13
  N13: Componente1.D10_PWM/SS, M1.IO5
  N14: Componente1.D11_PWM/MOSI, M1.IO23
  N15: Componente1.D12/MISO, M1.IO19
  N16: Componente1.D13/SCK, M1.IO18
  GND: Componente1.GND, M1.GND
  N17: Componente1.AREF, Componente1.RESET, M1.RST
  N18: Componente1.D0/RX, M1.RX0
  N19: Componente1.D1/TX, M1.TX0
  N20: Componente1.D2, M1.IO26
  N21: Componente1.D3_PWM, M1.IO25
  N22: Componente1.D4, M1.IO17
  N23: Componente1.D5_PWM, M1.IO16
  N24: Componente1.D6_PWM, M1.IO27
  N25: Componente1.D7, M1.IO14
  5V: Componente1.ioref, Componente1.5V, M1.5V
  3V3: Componente1.3V3, M1.3V3
  N26: Componente1.VIN, M1.VN
  N27: Componente1.N/C, M1.IOO

custom parts:
  Keyes Relay: The Keyes 5V relay module is suitable for SCM development, home appliance control. It uses a 5V~12V TIL control signal which can control DC / AC signal.
  >Wemos D1 R32: Wemos D1 R32 - This board is used with dual-mode Wi-Fi and Bluetooth chips, which is safe, reliable, and scalable to a variety of applications. DC in 5V-12V, 1 analog input(3.2V max input), a Micro USB connection, Compatible with D1 R32=WiFi+bluetooth+UNO
