# Fritzing sketch wemos - medidor - humedad - LCD - DHT11 (saved by Fritzing 0.9.10b)

parts:
  KY-1 = Keyes Relay [package=THT]
  Componente1 = Arduino Uno (Rev3)
  M1 = >Wemos D1 R32
  Mod1 = Arduino Sensor Shield v5.0
  U1 = Vibration Motor- ROB-08449 [package=vibe-motor-10mm]
  Componente2 = Soil Moisture Sensor
  Componente3 = LCD1602-I2C
  DHT11_1 = DHT11 module

nets:
  N1: KY-1.signal, Mod1.2-S, Mod1.ParallelLCD-D2
  VCC: KY-1.power, KY-1.C, Mod1.VCC, Mod1.A1-VCC, Mod1.IIC-VCC, Mod1.7-V, Mod1.2-V, Mod1.SerialLCD-VCC, Componente2.VCC, Componente3.VCC, DHT11_1.VCC
  GND: KY-1.ground, Mod1.GND, Mod1.A1-GND, Mod1.IIC-GND, Mod1.7-G, Mod1.2-G, Mod1.SerialLCD-GND, U1.+, Componente2.GND, Componente3.GND, DHT11_1.GND
  N2: KY-1.NO, U1.-
  N3: Componente1.A0, M1.IO2
  N4: Componente1.A1, M1.IO4
  N5: Componente1.A2, M1.IO35
  N6: Componente1.A3, M1.IO34
  N7: Componente1.A4/SDA, M1.IO36, M1.SDA
  N8: Componente1.A5/SCL, M1.IO39, M1.SCL
  N9: Componente1.D8, M1.IO12
  N10: Componente1.D9_PWM, M1.IO13
  N11: Componente1.D10_PWM/SS, M1.IO5
  N12: Componente1.D11_PWM/MOSI, M1.IO23
  N13: Componente1.D12/MISO, M1.IO19
  N14: Componente1.D13/SCK, M1.IO18
  GND_2: Componente1.GND, M1.GND
  N15: Componente1.AREF, Componente1.RESET, M1.RST
  N16: Componente1.D0/RX, M1.RX0
  N17: Componente1.D1/TX, M1.TX0
  N18: Componente1.D2, M1.IO26
  N19: Componente1.D3_PWM, M1.IO25
  N20: Componente1.D4, M1.IO17
  N21: Componente1.D5_PWM, M1.IO16
  N22: Componente1.D6_PWM, M1.IO27
  N23: Componente1.D7, M1.IO14
  5V: Componente1.ioref, Componente1.5V, M1.5V
  3V3: Componente1.3V3, M1.3V3
  N24: Componente1.VIN, M1.VN
  N25: Componente1.N/C, M1.IOO
  N26: Mod1.URF01-A1, Mod1.A1-SIG, Componente2.SIG
  N27: Mod1.A4-SIG, Mod1.IIC-SDA, Componente3.SDA
  N28: Mod1.A5-SIG, Mod1.IIC-SCL, Componente3.SCL
  N29: Mod1.7-S, Mod1.ParallelLCD-D7, DHT11_1.DATA

custom parts:
  Keyes Relay: The Keyes 5V relay module is suitable for SCM development, home appliance control. It uses a 5V~12V TIL control signal which can control DC / AC signal.
  >Wemos D1 R32: Wemos D1 R32 - This board is used with dual-mode Wi-Fi and Bluetooth chips, which is safe, reliable, and scalable to a variety of applications. DC in 5V-12V, 1 analog input(3.2V max input), a Micro USB connection, Compatible with D1 R32=WiFi+bluetooth+UNO
  LCD1602-I2C: A standard character display, usually with 2x16 characters. Comes in many colors with LCM1602 IIC attached.
  DHT11 module: https://cdn-learn.adafruit.com/downloads/pdf/dht.pdf DHT11 black pcb module reference by:https://github.com/adafruit/Fritzing-Library/blob/master/parts/DHT11%20Humitidy%20and%20Temperature%20Sensor.fzpz
